# Fritzing sketch 7-segments via shift register (saved by Fritzing 0.9.1b)
breadboards: 1

parts:
  7_Segment1 = 7 Segment Display
  Part1 = Arduino Uno (Rev3)
  U1 = 74HC595 [package="DIP16 [THT]"]
  R1 = Resistor [tolerance=±5% resistance=330 package=THT]
  R2 = Resistor [tolerance=±5% resistance=330 package=THT]
  R3 = Resistor [tolerance=±5% resistance=330 package=THT]
  R4 = Resistor [tolerance=±5% resistance=330 package=THT]
  R5 = Resistor [tolerance=±5% resistance=330 package=THT]
  R6 = Resistor [tolerance=±5% resistance=330 package=THT]
  R7 = Resistor [tolerance=±5% resistance=330 package=THT]
  R8 = Resistor [tolerance=±5% resistance=330 package=THT]

nets:
  N1: 7_Segment1.Segment_E, R5.Pin_1
  N2: 7_Segment1.Segment_D, R4.Pin_1
  5V: 7_Segment1.common_anode, Part1.5V, U1.MR, U1.VCC
  N3: 7_Segment1.Segment_C, R3.Pin_1
  N4: 7_Segment1.Segment_DP, R8.Pin_1
  N5: 7_Segment1.Segment_B, R2.Pin_1
  N6: 7_Segment1.Segment_F, R6.Pin_1
  N7: 7_Segment1.Segment_G, R7.Pin_1
  GND: Part1.GND, U1.GND, U1.OE
  N8: Part1.D2, U1.DS
  N9: Part1.D3_PWM, U1.ST_CP
  N10: Part1.D4, U1.SH_CP
  N11: U1.Q1, R2.Pin_0
  N12: U1.Q2, R3.Pin_0
  N13: U1.Q3, R4.Pin_0
  N14: U1.Q4, R5.Pin_0
  N15: U1.Q5, R6.Pin_0
  N16: U1.Q6, R7.Pin_0
  N17: U1.Q7, R8.Pin_0
  N18: U1.Q0, R1.Pin_0
