# Fritzing sketch Keypad Board (saved by Fritzing 0.8.7b)
circuit board: 5.64444cm x 8.46667cm
perfboards: 1

parts:
  S1 = Pushbutton [package="[THT]"]
  R1 = Resistor [tolerance=±5% resistance=10k package=THT]
  S2 = Pushbutton [package="[THT]"]
  R2 = Resistor [tolerance=±5% resistance=10k package=THT]
  S3 = Pushbutton [package="[THT]"]
  S4 = Pushbutton [package="[THT]"]
  S5 = Pushbutton [package="[THT]"]
  S6 = Pushbutton [package="[THT]"]
  S7 = Pushbutton [package="[THT]"]
  S8 = Pushbutton [package="[THT]"]
  S9 = Pushbutton [package="[THT]"]
  S10 = Pushbutton [package="[THT]"]
  R3 = Resistor [tolerance=±5% resistance=10k package=THT]
  R4 = Resistor [tolerance=±5% resistance=10k package=THT]
  R5 = Resistor [tolerance=±5% resistance=10k package=THT]
  R6 = Resistor [tolerance=±5% resistance=10k package=THT]
  R7 = Resistor [tolerance=±5% resistance=10k package=THT]
  R8 = Resistor [tolerance=±5% resistance=10k package=THT]
  R9 = Resistor [tolerance=±5% resistance=10k package=THT]
  R10 = Resistor [tolerance=±5% resistance=10k package=THT]
  J1 = double row rounded female pin header, 16 pins [form="♀ (female rounded)"]
  J2 = double row male pin header, 12 pins [form="♂ (male)"]
  IC1 = CD74HC4067E [package="DIP (Dual Inline) [THT]"]

nets:
  5V: S1.Pin_1, S1.Pin_2, S2.Pin_1, S2.Pin_2, S3.Pin_1, S3.Pin_2, S4.Pin_1, S4.Pin_2, S5.Pin_1, S5.Pin_2, S6.Pin_1, S6.Pin_2, S7.Pin_1, S7.Pin_2, S8.Pin_1, S8.Pin_2, S9.Pin_1, S9.Pin_2, S10.Pin_1, S10.Pin_2, J1.pin1, J2.pin1, IC1.Vcc
  N1: S1.Pin_3, S1.Pin_4, R1.Pin_0, IC1.I1
  GND: R1.Pin_1, R2.Pin_1, R3.Pin_1, R4.Pin_1, R5.Pin_1, R6.Pin_1, R7.Pin_1, R8.Pin_1, R9.Pin_1, R10.Pin_1, J1.pin2, J2.pin2, IC1.GND, IC1.E, IC1.I15, IC1.I14
  N2: S2.Pin_3, S2.Pin_4, R2.Pin_0, IC1.I4
  N3: S3.Pin_3, S3.Pin_4, R3.Pin_0, IC1.I7
  N4: S4.Pin_3, S4.Pin_4, R4.Pin_0, IC1.I0
  N5: S5.Pin_3, S5.Pin_4, R5.Pin_0, IC1.I3
  N6: S6.Pin_3, S6.Pin_4, R6.Pin_0, IC1.I6
  N7: S7.Pin_3, S7.Pin_4, R7.Pin_0, IC1.I13
  N8: S8.Pin_3, S8.Pin_4, R8.Pin_0, IC1.I2
  N9: S9.Pin_3, S9.Pin_4, R9.Pin_0, IC1.I5
  N10: S10.Pin_3, S10.Pin_4, R10.Pin_0, IC1.I9
  N11: J1.pin3, IC1.COM
  N12: J1.pin4, IC1.S0
  N13: J1.pin5, IC1.S1
  N14: J1.pin6, IC1.S2
  N15: J1.pin7, IC1.S3
  N16: J1.pin8, J2.pin8
  N17: J1.pin9, J2.pin7
  N18: J1.pin10, J2.pin6
  N19: J1.pin11, J2.pin5
  N20: J1.pin12, J2.pin4
  N21: J1.pin13, J2.pin3
  N22: J2.pin9, IC1.I8
  N23: J2.pin10, IC1.I12
  N24: J2.pin11, IC1.I11
  N25: J2.pin12, IC1.I10

notes:
  KEYPAD BOARD
  FOR MAKS & ALEX

custom parts:
  CD74HC4067E: High-Speed CMOS Logic 16-Channel Analog Multiplexer/Demultiplexer
