# Fritzing sketch PCB (saved by Fritzing 0.9.0b)
breadboards: 1

parts:
  Q1 = Basic FET N-Channel [package="TO220 [THT]"]
  Q2 = Basic FET N-Channel [package="TO220 [THT]"]
  Q3 = Basic FET N-Channel [package="TO220 [THT]"]
  R1 = Resistor [tolerance=±5% resistance=150 package=THT]
  R2 = Resistor [tolerance=±5% resistance=150 package=THT]
  R3 = Resistor [tolerance=±5% resistance=150 package=THT]
  J1 = male pin header, 5 pins [form="♂ (male)"]
  J2 = male pin header, 5 pins [form="♂ (male)"]

nets:
  N1: Q1.gate, R1.Pin_1
  N2: Q1.drain, J2.pin2
  GND: Q1.source, Q2.source, Q3.source, J1.pin5, J2.pin5
  N3: Q2.gate, R2.Pin_1
  N4: Q2.drain, J2.pin3
  N5: Q3.gate, R3.Pin_1
  N6: Q3.drain, J2.pin4
  N7: R1.Pin_0, J1.pin2
  N8: R2.Pin_0, J1.pin3
  N9: R3.Pin_0, J1.pin4
  12V: J1.pin1, J2.pin1
