# Fritzing sketch ControlBoard PCB (saved by Fritzing 0.9.2b)
perfboards: 1

parts:
  LED1 = LED - 5mm [color="Red (633nm)" package="5 mm [THT]"]
  LED2 = LED - 5mm [color="Yellow (595nm)" package="5 mm [THT]"]
  LED3 = LED - 5mm [color="Green (565nm)" package="5 mm [THT]"]
  ANALOG_IN = male pin header, 6 pins [form="♂ (male)"]
  POWER = male pin header, 8 pins [form="♂ (male)"]
  DIGITAL1 = male pin header, 8 pins [form="♂ (male)"]
  S1 = Pushbutton [package="[THT]"]
  R3 = Resistor [tolerance=±5% resistance=10k package=THT]
  SENSOR = male pin header, 2 pins [form="♂ (male)"]
  ALARM_LED = male pin header, 2 pins [form="♂ (male)"]
  R4 = Resistor [tolerance=±5% resistance=270 package=THT]
  SPKR = male pin header, 2 pins [form="♂ (male)"]
  R5 = Resistor [tolerance=±5% resistance=270 package=THT]

nets:
  N1: LED1.cathode, LED2.cathode, LED3.cathode, R5.Pin_1
  N2: LED1.anode, DIGITAL1.pin6
  N3: LED2.anode, DIGITAL1.pin5
  N4: LED3.anode, DIGITAL1.pin4
  N5: ANALOG_IN.pin1, R3.Pin_0, SENSOR.pin1
  5V: POWER.pin4, SENSOR.pin2
  GND: POWER.pin7, S1.Pin_3, S1.Pin_4, R3.Pin_1, R4.Pin_1, SPKR.pin1, R5.Pin_0
  N6: DIGITAL1.pin3, S1.Pin_1, S1.Pin_2
  N7: DIGITAL1.pin7, SPKR.pin2
  N8: DIGITAL1.pin8, ALARM_LED.pin1
  N9: ALARM_LED.pin2, R4.Pin_0
