# Fritzing sketch ControlBoard Prototype (saved by Fritzing 0.9.2b)
breadboards: 1

parts:
  LED1 = LED - 5mm [color="Red (633nm)" package="5 mm [THT]"]
  LED2 = LED - 5mm [color="Yellow (595nm)" package="5 mm [THT]"]
  LED3 = LED - 5mm [color="Green (565nm)" package="5 mm [THT]"]
  R1 = Resistor [tolerance=±5% resistance=220 package=THT]
  ANALOG_IN = male pin header, 6 pins [form="♂ (male)"]
  POWER = male pin header, 8 pins [form="♂ (male)"]
  DIGITAL1 = male pin header, 8 pins [form="♂ (male)"]
  DIGITAL2 = male pin header, 11 pins [form="♂ (male)"]  # not connected
  R2 = Photocell (LDR) [package=THT]
  SPKR1 = Loudspeaker
  S1 = Pushbutton [package="[THT]"]
  R3 = Resistor [tolerance=±5% resistance=10k package=THT]

nets:
  N1: LED1.cathode, LED2.cathode, LED3.cathode, R1.Pin_1
  N2: LED1.anode, DIGITAL1.pin6
  N3: LED2.anode, DIGITAL1.pin5
  N4: LED3.anode, DIGITAL1.pin4
  GND: R1.Pin_0, POWER.pin7, SPKR1.pin2, S1.Pin_3, S1.Pin_4, R3.Pin_1
  N5: ANALOG_IN.pin1, R2.pin_1, R3.Pin_0
  5V: POWER.pin4, R2.pin_0
  N6: DIGITAL1.pin3, S1.Pin_1, S1.Pin_2
  N7: DIGITAL1.pin7, SPKR1.pin1
